// Logisim project ALUBUENO.circ as structural Verilog: 1 circuit, main circuit main
module main (
  input  [3:0] ALUControl,
  input  [15:0] A,
  input  [15:0] B,
  output zero,
  output [15:0] Result
);

  wire [15:0] adder_1_out, and_1_out, not_1_out, or_1_out, subtractor_1_out;

  assign not_1_out = ~A;  // NOT_Gate not_1, 16 bits wide
  Adder #(.width(16)) adder_1 (.a(A), .b(B), .out(adder_1_out));  // open: cin, cout
  Subtractor #(.width(16)) subtractor_1 (.a(A), .b(B), .out(subtractor_1_out));  // open: bin, bout
  nor nor_1 (zero, A[0], A[1], A[2], A[3], A[4], A[5], A[6], A[7], A[8], A[9], A[10], A[11], A[12], A[13], A[14], A[15]);
  assign and_1_out = A & B;  // AND_Gate and_1, 16 bits wide
  assign or_1_out = A | B;  // OR_Gate or_1, 16 bits wide
  Multiplexer #(.select(4), .width(16), .enable("false")) multiplexer_1 (
    .in0(adder_1_out), .in1(subtractor_1_out), .in2(and_1_out), .in3(or_1_out), .in4(not_1_out),
    .out(Result), .sel(ALUControl));  // open: in5, in6, in7, in8, in9, in10, in11, in12, in13, in14, in15
endmodule
