// Logisim project CPU.circ as structural Verilog: 4 circuits, main circuit main
module main (
);

  wire alu_1_zero, clock_1_out, control_1_alusrc, control_1_jr, control_1_mem2reg, control_1_memread,
       control_1_memwrite, control_1_regwrite;
  wire [1:0] control_1_datasrc;
  wire [2:0] control_1_pcsrc;
  wire [3:0] control_1_aluop;
  wire [15:0] adder_1_out, adder_2_out, alu_1_result, bit_extender_1_out, bit_extender_2_out,
       multiplexer_1_out, multiplexer_2_out, multiplexer_3_out, multiplexer_4_out, multiplexer_5_out,
       multiplexer_6_out, multiplexer_7_out, multiplexer_8_out, PC_q, ram_1_data, ram_2_data,
       registerfile_circ_1_rd_2, registerfile_circ_1_rs_2, registerfile_circ_1_rt_2;

  Multiplexer #(.width(16), .enable("false")) multiplexer_1 (
    .in0(adder_1_out), .in1(registerfile_circ_1_rd_2), .out(multiplexer_1_out), .sel(control_1_jr));
  Adder #(.width(16)) adder_1 (.a(PC_q), .b(multiplexer_2_out), .out(adder_1_out));  // open: cin, cout
  Clock clock_1 (.out(clock_1_out));
  Register #(.width(16), .trigger("falling")) PC (.D(multiplexer_1_out), .Q(PC_q), .clk(clock_1_out));  // open: en, clr
  Multiplexer #(.select(3), .width(16), .enable("false")) multiplexer_2 (
    .in0(16'h1), .in1(bit_extender_1_out), .in2(bit_extender_1_out), .in3(multiplexer_3_out),
    .in4(multiplexer_4_out), .in5(bit_extender_2_out), .out(multiplexer_2_out), .sel(control_1_pcsrc));  // open: in6, in7
  Adder #(.width(16)) adder_2 (.a(PC_q), .b(16'h1), .out(adder_2_out));  // open: cin, cout
  RAM #(.addrWidth(16), .dataWidth(16)) ram_1 (
    .addr(PC_q), .data(ram_1_data), .clk(clock_1_out));  // open: sel, ld, clr
  // Probe on ram_1_data[15:12]
  Multiplexer #(.width(16), .enable("false")) multiplexer_3 (
    .in0(16'h1), .in1(bit_extender_1_out), .out(multiplexer_3_out), .sel(alu_1_zero));
  Multiplexer #(.width(16), .enable("false")) multiplexer_4 (
    .in0(bit_extender_1_out), .in1(16'h1), .out(multiplexer_4_out), .sel(alu_1_zero));
  assign bit_extender_1_out = {{8{ram_1_data[7]}}, ram_1_data[7:0]};  // Bit_Extender bit_extender_1
  Multiplexer #(.select(2), .width(16), .enable("false")) multiplexer_5 (
    .in0(multiplexer_8_out), .in1(adder_2_out), .in2({ram_1_data[7:0], {8{1'b0}}}), .out(multiplexer_5_out),
    .sel(control_1_datasrc));  // open: in3
  RegisterFile_circ registerfile_circ_1 (
    .rt(ram_1_data[3:0]), .rs(ram_1_data[7:4]), .rd(ram_1_data[11:8]), .rt_2(registerfile_circ_1_rt_2),
    .rs_2(registerfile_circ_1_rs_2), .rd_2(registerfile_circ_1_rd_2), .Data(multiplexer_5_out),
    .clock(clock_1_out), .writeEnable(control_1_regwrite));
  assign bit_extender_2_out = {{4{ram_1_data[11]}}, ram_1_data[11:0]};  // Bit_Extender bit_extender_2
  Multiplexer #(.width(16), .enable("false")) multiplexer_6 (
    .in0(registerfile_circ_1_rt_2), .in1(registerfile_circ_1_rd_2), .out(multiplexer_6_out),
    .sel(control_1_alusrc));
  Multiplexer #(.width(16), .enable("false")) multiplexer_7 (
    .in0(registerfile_circ_1_rs_2), .in1(bit_extender_1_out), .out(multiplexer_7_out), .sel(control_1_alusrc));
  Multiplexer #(.width(16), .enable("false")) multiplexer_8 (
    .in0(alu_1_result), .in1(ram_2_data), .out(multiplexer_8_out), .sel(control_1_mem2reg));
  ALU alu_1 (
    .A(multiplexer_6_out), .B(multiplexer_7_out), .zero(alu_1_zero), .Result(alu_1_result),
    .ALUControl(control_1_aluop));
  Control control_1 (
    .OpCode(ram_1_data[15:12]), .MemRead(control_1_memread), .DataSrc(control_1_datasrc), .JR(control_1_jr),
    .Mem2Reg(control_1_mem2reg), .ALUOp(control_1_aluop), .MemWrite(control_1_memwrite),
    .ALUSrc(control_1_alusrc), .RegWrite(control_1_regwrite), .PCSrc(control_1_pcsrc));
  RAM #(.addrWidth(16), .dataWidth(16), .bus("separate")) ram_2 (
    .addr(alu_1_result), .din(registerfile_circ_1_rd_2), .data(ram_2_data), .str(control_1_memwrite),
    .clk(clock_1_out), .ld(control_1_memread));  // open: sel, clr
endmodule

module RegisterFile_circ (
  input  [15:0] Data,
  input  clock,
  input  writeEnable,
  input  [3:0] rt,
  input  [3:0] rs,
  input  [3:0] rd,
  output [15:0] rt_2,
  output [15:0] rs_2,
  output [15:0] rd_2
);

  wire and_1_out, and_2_out, and_3_out, and_4_out, and_5_out, and_6_out, and_7_out, and_8_out, and_9_out,
       and_10_out, and_11_out, and_12_out, and_13_out, and_14_out, and_15_out, and_16_out, and_17_out,
       decoder_1_out0, decoder_1_out1, decoder_1_out2, decoder_1_out3, decoder_1_out4, decoder_1_out5,
       decoder_1_out6, decoder_1_out7, decoder_1_out8, decoder_1_out9, decoder_1_out10, decoder_1_out11,
       decoder_1_out12, decoder_1_out13, decoder_1_out14, decoder_1_out15;
  wire [15:0] register_1_q, register_2_q, register_3_q, register_4_q, register_5_q, register_6_q,
       register_7_q, register_8_q, register_9_q, register_10_q, register_11_q, register_12_q, register_13_q,
       register_14_q, register_15_q, register_16_q;

  Decoder #(.select(4), .enable("false")) decoder_1 (
    .out0(decoder_1_out0), .out1(decoder_1_out1), .out2(decoder_1_out2), .out3(decoder_1_out3),
    .out4(decoder_1_out4), .out5(decoder_1_out5), .out6(decoder_1_out6), .out7(decoder_1_out7),
    .out8(decoder_1_out8), .out9(decoder_1_out9), .out10(decoder_1_out10), .out11(decoder_1_out11),
    .out12(decoder_1_out12), .out13(decoder_1_out13), .out14(decoder_1_out14), .out15(decoder_1_out15),
    .sel(rd));
  and and_1 (and_1_out, clock, writeEnable);
  and and_2 (and_2_out, and_1_out, decoder_1_out0);
  and and_3 (and_3_out, and_1_out, decoder_1_out1);
  and and_4 (and_4_out, and_1_out, decoder_1_out2);
  and and_5 (and_5_out, and_1_out, decoder_1_out3);
  and and_6 (and_6_out, and_1_out, decoder_1_out4);
  and and_7 (and_7_out, and_1_out, decoder_1_out5);
  and and_8 (and_8_out, and_1_out, decoder_1_out6);
  and and_9 (and_9_out, and_1_out, decoder_1_out7);
  and and_10 (and_10_out, and_1_out, decoder_1_out8);
  and and_11 (and_11_out, and_1_out, decoder_1_out9);
  and and_12 (and_12_out, and_1_out, decoder_1_out10);
  and and_13 (and_13_out, and_1_out, decoder_1_out11);
  and and_14 (and_14_out, and_1_out, decoder_1_out12);
  and and_15 (and_15_out, and_1_out, decoder_1_out13);
  and and_16 (and_16_out, and_1_out, decoder_1_out14);
  and and_17 (and_17_out, and_1_out, decoder_1_out15);
  Register #(.width(16)) register_1 (.D(Data), .Q(register_1_q), .clk(and_2_out));  // open: en, clr
  Register #(.width(16)) register_2 (.D(Data), .Q(register_2_q), .clk(and_3_out));  // open: en, clr
  Register #(.width(16)) register_3 (.D(Data), .Q(register_3_q), .clk(and_4_out));  // open: en, clr
  Register #(.width(16)) register_4 (.D(Data), .Q(register_4_q), .clk(and_5_out));  // open: en, clr
  Register #(.width(16)) register_5 (.D(Data), .Q(register_5_q), .clk(and_6_out));  // open: en, clr
  Register #(.width(16)) register_6 (.D(Data), .Q(register_6_q), .clk(and_7_out));  // open: en, clr
  Register #(.width(16)) register_7 (.D(Data), .Q(register_7_q), .clk(and_8_out));  // open: en, clr
  Register #(.width(16)) register_8 (.D(Data), .Q(register_8_q), .clk(and_9_out));  // open: en, clr
  Register #(.width(16)) register_9 (.D(Data), .Q(register_9_q), .clk(and_10_out));  // open: en, clr
  Register #(.width(16)) register_10 (.D(Data), .Q(register_10_q), .clk(and_11_out));  // open: en, clr
  Register #(.width(16)) register_11 (.D(Data), .Q(register_11_q), .clk(and_12_out));  // open: en, clr
  Register #(.width(16)) register_12 (.D(Data), .Q(register_12_q), .clk(and_13_out));  // open: en, clr
  Register #(.width(16)) register_13 (.D(Data), .Q(register_13_q), .clk(and_14_out));  // open: en, clr
  Register #(.width(16)) register_14 (.D(Data), .Q(register_14_q), .clk(and_15_out));  // open: en, clr
  Register #(.width(16)) register_15 (.D(Data), .Q(register_15_q), .clk(and_16_out));  // open: en, clr
  Register #(.width(16)) register_16 (.D(Data), .Q(register_16_q), .clk(and_17_out));  // open: en, clr
  Multiplexer #(.select(4), .width(16), .enable("false")) multiplexer_1 (
    .in0(register_1_q), .in1(register_2_q), .in2(register_3_q), .in3(register_4_q), .in4(register_5_q),
    .in5(register_6_q), .in6(register_7_q), .in7(register_8_q), .in8(register_9_q), .in9(register_10_q),
    .in10(register_11_q), .in11(register_12_q), .in12(register_13_q), .in13(register_14_q),
    .in14(register_15_q), .in15(register_16_q), .out(rt_2), .sel(rt));
  Multiplexer #(.select(4), .width(16), .enable("false")) multiplexer_2 (
    .in0(register_1_q), .in1(register_2_q), .in2(register_3_q), .in3(register_4_q), .in4(register_5_q),
    .in5(register_6_q), .in6(register_7_q), .in7(register_8_q), .in8(register_9_q), .in9(register_10_q),
    .in10(register_11_q), .in11(register_12_q), .in12(register_13_q), .in13(register_14_q),
    .in14(register_15_q), .in15(register_16_q), .out(rs_2), .sel(rs));
  Multiplexer #(.select(4), .width(16)) multiplexer_3 (
    .in0(register_1_q), .in1(register_2_q), .in2(register_3_q), .in3(register_4_q), .in4(register_5_q),
    .in5(register_6_q), .in6(register_7_q), .in7(register_8_q), .in8(register_9_q), .in9(register_10_q),
    .in10(register_11_q), .in11(register_12_q), .in12(register_13_q), .in13(register_14_q),
    .in14(register_15_q), .in15(register_16_q), .out(rd_2), .sel(rd));  // open: en
endmodule

module ALU (
  input  [3:0] ALUControl,
  input  [15:0] A,
  input  [15:0] B,
  output zero,
  output [15:0] Result
);

  wire [15:0] adder_1_out, and_1_out, not_1_out, or_1_out, subtractor_1_out;

  assign not_1_out = ~A;  // NOT_Gate not_1, 16 bits wide
  Adder #(.width(16)) adder_1 (.a(A), .b(B), .out(adder_1_out));  // open: cin, cout
  Subtractor #(.width(16)) subtractor_1 (.a(A), .b(B), .out(subtractor_1_out));  // open: bin, bout
  nor nor_1 (zero, A[0], A[1], A[2], A[3], A[4], A[5], A[6], A[7], A[8], A[9], A[10], A[11], A[12], A[13], A[14], A[15]);
  assign and_1_out = A & B;  // AND_Gate and_1, 16 bits wide
  assign or_1_out = A | B;  // OR_Gate or_1, 16 bits wide
  Multiplexer #(.select(4), .width(16), .enable("false")) multiplexer_1 (
    .in0(adder_1_out), .in1(subtractor_1_out), .in2(and_1_out), .in3(or_1_out), .in4(not_1_out),
    .out(Result), .sel(ALUControl));  // open: in5, in6, in7, in8, in9, in10, in11, in12, in13, in14, in15
endmodule

module Control (
  input  [3:0] OpCode,
  output MemRead,
  output [1:0] DataSrc,
  output JR,
  output Mem2Reg,
  output [3:0] ALUOp,
  output MemWrite,
  output ALUSrc,
  output RegWrite,
  output [2:0] PCSrc
);

  ROM #(.addrWidth(4), .dataWidth(15)) rom_1 (
    .addr(OpCode), .data({PCSrc, RegWrite, ALUSrc, MemWrite, ALUOp, Mem2Reg, JR, DataSrc, MemRead}));  // open: sel

  // Notes on the sheet:
  //   contents of rom_1 (hex, n*v repeats v):
  //   800 820 811 200 840 860 880 0 c00 804 3420 4420 0 0 200a 5000
endmodule
